# Fritzing sketch coeur platine (saved by Fritzing 0.9.3b)
breadboards: 1

parts:
  R1 = Resistor [tolerance=±5% resistance=220 package=THT]
  R2 = Resistor [tolerance=±5% resistance=220 package=THT]
  R3 = Resistor [tolerance=±5% resistance=220 package=THT]
  R4 = Resistor [tolerance=±5% resistance=220 package=THT]
  R5 = Resistor [tolerance=±5% resistance=220 package=THT]
  R6 = Resistor [tolerance=±5% resistance=220 package=THT]
  R7 = Resistor [tolerance=±5% resistance=220 package=THT]
  R8 = Resistor [tolerance=±5% resistance=220 package=THT]
  LED1 = LED - 5mm [color="Red (633nm)" package="5 mm [THT]"]
  LED2 = LED - 5mm [color="Red (633nm)" package="5 mm [THT]"]
  LED3 = LED - 5mm [color="Red (633nm)" package="5 mm [THT]"]
  LED4 = LED - 5mm [color="Red (633nm)" package="5 mm [THT]"]
  LED5 = LED - 5mm [color="Red (633nm)" package="5 mm [THT]"]
  LED6 = LED - 5mm [color="Red (633nm)" package="5 mm [THT]"]
  LED7 = LED - 5mm [color="Red (633nm)" package="5 mm [THT]"]
  LED8 = LED - 5mm [color="Red (633nm)" package="5 mm [THT]"]
  Composant1 = Arduino Uno (Rev3)

nets:
  N1: R1.Pin_0, R1.Pin_1, LED8.anode, Composant1.D12/MISO
  N2: R2.Pin_0, R2.Pin_1, LED7.anode, Composant1.D11_PWM/MOSI
  N3: R3.Pin_0, R3.Pin_1, LED6.anode, Composant1.D10_PWM/SS
  N4: R4.Pin_0, R4.Pin_1, LED5.anode, Composant1.D9_PWM
  N5: R5.Pin_0, R5.Pin_1, LED3.anode, Composant1.D3_PWM
  N6: R6.Pin_0, R6.Pin_1, LED4.anode, Composant1.D2
  N7: R7.Pin_0, R7.Pin_1, LED2.anode, Composant1.D5_PWM
  N8: R8.Pin_0, R8.Pin_1, LED1.anode, Composant1.D6_PWM
  N9: LED1.cathode, LED2.cathode, LED3.cathode, LED4.cathode, LED5.cathode, LED6.cathode, LED7.cathode, LED8.cathode, Composant1.GND
