# Fritzing sketch schema Coeur Leds (saved by Fritzing 0.9.3b)
breadboards: 1

parts:
  Composant1 = Arduino Uno (Rev3)
  R1 = Resistor [tolerance=±5% resistance=220 package=THT]
  LED1 = LED - 5mm [color="Red (633nm)" package="5 mm [THT]"]
  LED3 = LED - 5mm [color="Red (633nm)" package="5 mm [THT]"]
  LED4 = LED - 5mm [color="Red (633nm)" package="5 mm [THT]"]
  LED5 = LED - 5mm [color="Red (633nm)" package="5 mm [THT]"]
  LED6 = LED - 5mm [color="Red (633nm)" package="5 mm [THT]"]
  LED7 = LED - 5mm [color="Red (633nm)" package="5 mm [THT]"]
  LED8 = LED - 5mm [color="Red (633nm)" package="5 mm [THT]"]
  LED9 = LED - 5mm [color="Red (633nm)" package="5 mm [THT]"]
  LED10 = LED - 5mm [color="Red (633nm)" package="5 mm [THT]"]
  LED11 = LED - 5mm [color="Red (633nm)" package="5 mm [THT]"]
  LED12 = LED - 5mm [color="Red (633nm)" package="5 mm [THT]"]
  LED13 = LED - 5mm [color="Red (633nm)" package="5 mm [THT]"]

nets:
  N1: Composant1.D2, R1.Pin_1
  N2: Composant1.GND, LED1.cathode
  N3: R1.Pin_0, LED3.anode
  N4: LED1.anode, LED5.cathode
  N5: LED3.cathode, LED4.anode
  N6: LED4.cathode, LED6.anode
  N7: LED5.anode, LED11.cathode
  N8: LED6.cathode, LED7.anode
  N9: LED7.cathode, LED8.anode
  N10: LED8.cathode, LED9.anode
  N11: LED9.cathode, LED10.anode
  N12: LED10.cathode, LED13.anode
  N13: LED11.anode, LED12.cathode
  N14: LED12.anode, LED13.cathode
