# Fritzing sketch shématique (saved by Fritzing 0.9.3b)
breadboards: 1

parts:
  Q1 = NPN-Transistor [package="TO92 [THT]"]
  R1 = Resistor [tolerance=±5% resistance=18 package=THT]
  C1 = Electrolytic Capacitor [capacitance=1µF package="100 mil [THT, electrolytic]"]
  U1 = LM124-324 Quad Opamp [package="DIP (Dual Inline)"]
  C2 = Ceramic Capacitor [capacitance=0.1µF package="100 mil [THT, multilayer]"]
  R2 = Resistor [tolerance=±5% resistance=220 package=THT]
  R3 = Resistor [tolerance=±5% resistance=68k package=THT]
  C3 = Ceramic Capacitor [capacitance=0.1µF package="100 mil [THT, multilayer]"]
  R4 = Resistor [tolerance=±5% resistance=8.2k package=THT]
  C4 = Electrolytic Capacitor [capacitance=1µF package="100 mil [THT, electrolytic]"]
  R5 = Resistor [tolerance=±5% resistance=68k package=THT]
  R6 = Resistor [tolerance=±5% resistance=39k package=THT]
  Q2 = PHOTOTRANSISTOR REFLECTIVE OBJECT SENSOR [package=qrb1114-side]
  R7 = Resistor [tolerance=±5% resistance=220 package=THT]
  Composant1 = Arduino Uno (Rev3)

nets:
  N1: Q1.E, Composant1.A0
  N2: Q1.C, U1.VCC+, R6.Pin_1, R7.Pin_1, Composant1.5V
  N3: R1.Pin_0, U1.4OUT, C2.1
  N4: C1.-, U1.4IN+, R3.Pin_0
  N5: C1.+, U1.1OUT, C3.1
  N6: U1.1IN-, C3.0, R4.Pin_1
  N7: U1.1IN+, C4.-, R5.Pin_1
  GND: U1.VCC-, Q2.E, Q2.K
  N8: C2.0, R2.Pin_1
  N9: C4.+, Q2.A
