# Fritzing sketch schématique coeur (saved by Fritzing 0.9.3b)
breadboards: 1

parts:
  Composant1 = Arduino Uno (Rev3)
  LED1 = LED - 5mm [color="Red (633nm)" package="5 mm [THT]"]
  R1 = Resistor [tolerance=±5% resistance=220 package=THT]
  LED2 = LED - 5mm [color="Red (633nm)" package="5 mm [THT]"]
  R2 = Resistor [tolerance=±5% resistance=220 package=THT]
  R3 = Resistor [tolerance=±5% resistance=220 package=THT]
  LED3 = LED - 5mm [color="Red (633nm)" package="5 mm [THT]"]
  LED4 = LED - 5mm [color="Red (633nm)" package="5 mm [THT]"]
  R4 = Resistor [tolerance=±5% resistance=220 package=THT]
  R5 = Resistor [tolerance=±5% resistance=220 package=THT]
  LED5 = LED - 5mm [color="Red (633nm)" package="5 mm [THT]"]
  LED6 = LED - 5mm [color="Red (633nm)" package="5 mm [THT]"]
  R6 = Resistor [tolerance=±5% resistance=220 package=THT]
  R7 = Resistor [tolerance=±5% resistance=220 package=THT]
  LED7 = LED - 5mm [color="Red (633nm)" package="5 mm [THT]"]
  R8 = Resistor [tolerance=±5% resistance=220 package=THT]
  LED8 = LED - 5mm [color="Red (633nm)" package="5 mm [THT]"]

nets:
  N1: Composant1.D8, R5.Pin_0
  N2: Composant1.D9_PWM, R4.Pin_0
  N3: Composant1.D10_PWM/SS, R3.Pin_0
  N4: Composant1.D11_PWM/MOSI, R2.Pin_0
  N5: Composant1.D12/MISO, R1.Pin_0
  N6: Composant1.GND, LED1.cathode, LED2.cathode, LED3.cathode, LED4.cathode, LED5.cathode, LED6.cathode, LED7.cathode, LED8.cathode
  N7: Composant1.D5_PWM, R8.Pin_0
  N8: Composant1.D6_PWM, R7.Pin_0
  N9: Composant1.D7, R6.Pin_0
  N10: LED1.anode, R1.Pin_1
  N11: LED2.anode, R2.Pin_1
  N12: R3.Pin_1, LED3.anode
  N13: LED4.anode, R4.Pin_1
  N14: R5.Pin_1, LED5.anode
  N15: LED6.anode, R6.Pin_1
  N16: R7.Pin_1, LED7.anode
  N17: R8.Pin_1, LED8.anode
